# Fritzing sketch endpoint_circuit (saved by Fritzing 0.9.3b)
breadboards: 1

parts:
  Part1 = Bluetooth HM-10
  Part2 = InvenSense MPU6050
  Part3 = Arduino Nano (Rev3.0)

nets:
  N1: Part1.RXD, Part3.D2
  N2: Part1.TXD, Part3.D3
  GND: Part1.GND, Part2.GND, Part3.GND
  VCC: Part1.VCC, Part2.VCC, Part3.5V
  N3: Part2.SDA, Part3.A4
